# Fritzing sketch CricketChirper (saved by Fritzing 0.9.2b)
circuit board: 4.69147cm x 4.50542cm
breadboards: 1

parts:
  IC1 = Hex Inverter Schmitt Trigger SN74HC14 [package="DIP (Dual Inline)"]
  D1 = Diode [package=diode-1n4148]
  D2 = Diode [package=diode-1n4148]
  C4 = Electrolytic Capacitor [capacitance=100µF package="200 mil [THT, electrolytic]"]
  C1 = Ceramic Capacitor [capacitance="100 nF" package="200 mil [THT, multilayer]"]
  R1 = Resistor [tolerance=±5% resistance=100k package=THT]
  R2 = Resistor [tolerance=±5% resistance=390k package=THT]
  C2 = Ceramic Capacitor [capacitance=1µF package="200 mil [THT, multilayer]"]
  R3 = Resistor [tolerance=±5% resistance=2.9M package=THT]
  C3 = Ceramic Capacitor [capacitance=1µF package="200 mil [THT, multilayer]"]
  SPK = female pin header, 1 pin [form="♀ (female)"]
  GND = female pin header, 1 pin [form="♀ (female)"]
  Vcc = female pin header, 1 pin [form="♀ (female)"]

nets:
  N1: IC1.1A, IC1.2Y, R1.Pin_0, SPK.pin1
  N2: IC1.1Y, C1.1
  N3: IC1.2A, D1.C, C1.0, R1.Pin_1
  N4: IC1.3A, IC1.4Y, D1.A, R2.Pin_0
  N5: IC1.3Y, C2.1
  GND: IC1.GND, C4.-, GND.pin1
  N6: IC1.4A, D2.A, R2.Pin_1, C2.0
  N7: IC1.5Y, IC1.6A, D2.C, R3.Pin_0
  N8: IC1.5A, R3.Pin_1, C3.0
  N9: IC1.6Y, C3.1
  N10: IC1.VCC, C4.+, Vcc.pin1
